# Fritzing sketch first_one (saved by Fritzing 0.9.3b)
breadboards: 1

parts:
  Part1 = Arduino Pro Mini v13
  R1 = Resistor [tolerance=±5% resistance=80k package="2512 [SMD]"]
  R2 = Resistor [tolerance=±5% resistance=80k package="2512 [SMD]"]
  R3 = Resistor [tolerance=±5% resistance=80k package="2512 [SMD]"]
  R4 = Resistor [tolerance=±5% resistance=80k package="2512 [SMD]"]
  R5 = Resistor [tolerance=±5% resistance=80k package="2512 [SMD]"]
  R6 = Resistor [tolerance=±5% resistance=80k package="2512 [SMD]"]
  R7 = Resistor [tolerance=±5% resistance=80k package="2512 [SMD]"]
  R8 = Resistor [tolerance=±5% resistance=80k package="2512 [SMD]"]
  R9 = Resistor [tolerance=±5% resistance=80k package="2512 [SMD]"]
  LED1 = smd LED [color="Blue (470nm)" package="0805 [SMD]"]
  LED2 = smd LED [color="Blue (470nm)" package="0805 [SMD]"]
  LED3 = smd LED [color="Blue (470nm)" package="0805 [SMD]"]
  LED4 = smd LED [color="Blue (470nm)" package="0805 [SMD]"]
  LED5 = smd LED [color="Blue (470nm)" package="0805 [SMD]"]
  LED6 = smd LED [color="Blue (470nm)" package="0805 [SMD]"]
  LED7 = smd LED [color="Blue (470nm)" package="0805 [SMD]"]
  LED8 = smd LED [color="Blue (470nm)" package="0805 [SMD]"]
  LED9 = smd LED [color="Blue (470nm)" package="0805 [SMD]"]
  R10 = Photocell (LDR) [package=THT]
  R11 = Resistor [tolerance=±5% resistance=10k package=THT]
  Part2 = Power Cell LiPo Charger/Booster
  BAT1 = Battery Holders [package=lipo-1100mAh]
  Part3 = Solar Panel [package="Renogy 50 Watts 12 Volt Monocrystalline Bendable Solar Panel"]

nets:
  VCC: Part1.VCC, R10.pin_0, Part2.VCC
  GND: Part1.GND, LED1.cathode, LED2.cathode, LED3.cathode, LED4.cathode, LED5.cathode, LED6.cathode, LED7.cathode, LED8.cathode, LED9.cathode, R11.Pin_1, Part2.GND, BAT1.-, Part3.Connector_2
  N1: Part1.A0, R10.pin_1, R11.Pin_0
  N2: Part1.D10_PWM/SS, R9.Pin_0
  N3: Part1.D9_PWM, R8.Pin_0
  N4: Part1.D8, R7.Pin_0
  N5: Part1.D7, R6.Pin_0
  N6: Part1.D6_PWM, R5.Pin_0
  N7: Part1.D5_PWM, R4.Pin_0
  N8: Part1.D4, R3.Pin_0
  N9: Part1.D3_PWM, R2.Pin_0
  N10: Part1.D2, R1.Pin_0
  N11: R1.Pin_1, LED1.anode
  N12: R2.Pin_1, LED2.anode
  N13: R3.Pin_1, LED3.anode
  N14: R4.Pin_1, LED4.anode
  N15: R5.Pin_1, LED5.anode
  N16: R6.Pin_1, LED6.anode
  N17: R7.Pin_1, LED7.anode
  N18: R8.Pin_1, LED8.anode
  N19: R9.Pin_1, LED9.anode
  N20: Part2.5VIN, Part3.Connector_1
  N21: Part2.VBATT, BAT1.+

custom parts:
  Solar Panel: Renogy 50 Watts 12 Volt Solar Panel
